# Fritzing sketch arduino_dht22 (saved by Fritzing 0.9.3b)
circuit board: 8.46667cm x 5.64444cm
breadboards: 1

parts:
  U1 = atmega328 [package=dip]
  Part1 = NRF24L01+ Breakout Board
  J1 = Screw terminal - 2 pins [package=THT]
  J2 = double row female pin header, 8 pins [form="♀ (female)"]
  C3 = Ceramic Capacitor [capacitance=22pF package="100 mil [THT, multilayer]"]
  C4 = Electrolytic Capacitor [capacitance=10µF voltage=6.3V package="100 mil [THT, electrolytic]"]
  R1 = Resistor [tolerance=±5% resistance=10k package=THT]
  XTAL1 = Crystal [frequency="16 Mhz" package=THT]
  C2 = Ceramic Capacitor [capacitance=22pF package="100 mil [THT, multilayer]"]
  S1 = Momentary Switch [package=ksa_sealed_tac_switch]
  DHT22 = Humidity and Temperature Sensor RHT03
  J3 = double row female pin header, 8 pins [form="♀ (female)"]
  R2 = Resistor [tolerance=±5% resistance=10k package=THT]

nets (from the schematic view):
  N1: U1.RESET, R1.Pin_1, S1.3
  N2: U1.D4, J2.pin5
  VCC: U1.VCC, U1.AVCC, U1.AREF, J1.pin2, J2.pin8, C4.+, R1.Pin_0, DHT22.Vcc, R2.Pin_1
  GND: U1.GND#7, J1.pin1, J2.pin1, C3.0, C4.-, C2.0, S1.1, DHT22.GND_2
  N3: U1.XLAT1, C3.1, XTAL1.pin_1
  N4: U1.XLAT2, XTAL1.pin_0, C2.1
  N5: U1.D5_(PWM), DHT22.Data-signal, R2.Pin_0
  N6: U1.D7, J2.pin2
  N7: U1.D8, J2.pin7
  N8: U1.D11_(PWM), J2.pin6
  N9: U1.D12, J2.pin4
  N10: U1.D13, J2.pin3
  N11: Part1.GND, J3.pin1
  N12: Part1.VCC, J3.pin8
  N13: Part1.CE, J3.pin2
  N14: Part1.CS, J3.pin7
  N15: Part1.SCK, J3.pin3
  N16: Part1.MOSI, J3.pin6
  N17: Part1.MISO, J3.pin4
  N18: Part1.IRQ, J3.pin5
